// Logisim project floating_point_adder.circ as structural Verilog: 1 circuit, main circuit Main
module Main (
  input  [31:0] floatA,
  input  [31:0] floatB,
  output [31:0] result,
  output overflow,
  output underflow
);

  wire fracnum_adder_1_sig_overflow, full_pre_adder_1_are_sign_same, full_pre_adder_1_larger_sign;
  wire [9:0] full_pre_adder_1_larger_exp;
  wire [31:0] fracnum_adder_1_output_sig, full_pre_adder_1_larger_sig, full_pre_adder_1_smaller_sig;

  // Probe on full_pre_adder_1_larger_sig
  // Probe on full_pre_adder_1_smaller_sig
  // Probe on fracnum_adder_1_output_sig
  // Probe on full_pre_adder_1_larger_exp
  full_pre_adder full_pre_adder_1 (
    .float_A(floatA), .float_B(floatB), .are_sign_same(full_pre_adder_1_are_sign_same),
    .larger_sign(full_pre_adder_1_larger_sign), .larger_exp(full_pre_adder_1_larger_exp),
    .larger_sig(full_pre_adder_1_larger_sig), .smaller_sig(full_pre_adder_1_smaller_sig));
  fracnum_adder fracnum_adder_1 (
    .larger_sig(full_pre_adder_1_larger_sig), .smaller_sig(full_pre_adder_1_smaller_sig),
    .is_sign_same(full_pre_adder_1_are_sign_same), .output_sig(fracnum_adder_1_output_sig),
    .sig_overflow(fracnum_adder_1_sig_overflow));
  Normalizer normalizer_1 (
    .totalData(fracnum_adder_1_output_sig), .exponent(full_pre_adder_1_larger_exp),
    .largestSign(full_pre_adder_1_larger_sign), .carryOut(fracnum_adder_1_sig_overflow),
    .truncatedFloatingPoint(result), .overflow(overflow), .underflow(underflow));
endmodule
