// Logisim project phase2_add.circ as structural Verilog: 1 circuit, main circuit fracnum_adder
module fracnum_adder (
  input  [31:0] LargerFrac,
  input  [31:0] SmallerFrac,
  input  is_sign_same,
  output [31:0] OutputFrac,
  output FracOverflow
);

  wire [31:0] adder_1_out, subtractor_1_out;

  Subtractor #(.width(32)) subtractor_1 (.a(LargerFrac), .b(SmallerFrac), .out(subtractor_1_out));  // open: bin, bout
  Adder #(.width(32)) adder_1 (.a(LargerFrac), .b(SmallerFrac), .out(adder_1_out), .cout(FracOverflow));  // open: cin
  Multiplexer #(.width(32)) multiplexer_1 (
    .in0(subtractor_1_out), .in1(adder_1_out), .out(OutputFrac), .sel(is_sign_same));
endmodule
