// Logisim project phase3_post_add.circ as structural Verilog: 3 circuits, main circuit Normalizer
module Normalizer (
  input  [31:0] totalData,
  input  [9:0] exponent,
  input  largestSign,
  input  carryOut,
  output [31:0] truncatedFloatingPoint,
  output overflow,
  output underflow
);

  wire n7432_1_pin1, n7432_1_pin2, n7432_1_pin9, n7432_1_pin10, n7432_1_pin12;
  wire [4:0] priorityencoder_1_selectbit;
  wire [9:0] adder_1_out, multiplexer_1_out, subtractor_1_out;
  wire [31:0] multiplexer_2_out, shifter_1_out, shifter_2_out;
  wire [31:31] n7432_1_pin11;

  // Probe on truncatedFloatingPoint[30:21]
  // Probe on truncatedFloatingPoint[20:0]
  Shifter #(.shift("lr"), .width(32)) shifter_1 (.in(totalData), .\dist (5'b00001), .out(shifter_1_out));
  _7432 u_7432_1 (
    .pin1(n7432_1_pin1), .pin2(n7432_1_pin2), .pin3(overflow), .pin13(shifter_1_out[31]),
    .pin12(n7432_1_pin12), .pin11(n7432_1_pin11[31]), .pin10(n7432_1_pin10), .pin9(n7432_1_pin9),
    .pin8(underflow));  // open: pin4, pin5, pin6
  PriorityEncoder priorityencoder_1 (
    .dataBus(totalData), .selectBit(priorityencoder_1_selectbit), .underFlow(n7432_1_pin9));
  Adder #(.width(10)) adder_1 (.a(exponent), .b(10'h1), .out(adder_1_out), .cout(n7432_1_pin2));  // open: cin
  // Probe on shifter_2_out
  Shifter #(.width(32)) shifter_2 (.in(totalData), .\dist (priorityencoder_1_selectbit), .out(shifter_2_out));
  // Probe on {n7432_1_pin11[31], shifter_1_out[30:0]}
  Truncer truncer_1 (
    .in32bit(multiplexer_2_out), .inExp(multiplexer_1_out), .out21bit(truncatedFloatingPoint[20:0]),
    .outExp(truncatedFloatingPoint[30:21]), .overflow(n7432_1_pin1));
  // Probe on subtractor_1_out
  Subtractor #(.width(10)) subtractor_1 (
    .a(exponent), .b({{5{1'b0}}, priorityencoder_1_selectbit}), .out(subtractor_1_out), .bout(n7432_1_pin10));  // open: bin
  // Probe on subtractor_1_out
  Multiplexer #(.width(10)) multiplexer_1 (
    .in0(subtractor_1_out), .in1(adder_1_out), .out(multiplexer_1_out), .sel(carryOut));
  Multiplexer #(.width(32)) multiplexer_2 (
    .in0(shifter_2_out), .in1({n7432_1_pin11[31], shifter_1_out[30:0]}), .out(multiplexer_2_out),
    .sel(carryOut));

  assign truncatedFloatingPoint[31] = largestSign;
  // also tied to VCC on the sheet: n7432_1_pin12

  // Notes on the sheet:
  //   incremented exp
  //   decremented exp
  //   left shifted significant
  //   right shifted significant with MSB set to 1
  //   if adder produced carry, incremented exp with right shifted significant is selected
endmodule

module PriorityEncoder (
  input  [31:0] dataBus,
  output [4:0] selectBit,
  output underFlow
);

  wire priority_encoder_1_gs;
  wire [4:0] multiplexer_1_out, priority_encoder_1_out;

  Priority_Encoder #(.select(5)) priority_encoder_1 (
    .in0(dataBus[0]), .in1(dataBus[1]), .in2(dataBus[2]), .in3(dataBus[3]), .in4(dataBus[4]),
    .in5(dataBus[5]), .in6(dataBus[6]), .in7(dataBus[7]), .in8(dataBus[8]), .in9(dataBus[9]),
    .in10(dataBus[10]), .in11(dataBus[11]), .in12(dataBus[12]), .in13(dataBus[13]), .in14(dataBus[14]),
    .in15(dataBus[15]), .in16(dataBus[16]), .in17(dataBus[17]), .in18(dataBus[18]), .in19(dataBus[19]),
    .in20(dataBus[20]), .in21(dataBus[21]), .in22(dataBus[22]), .in23(dataBus[23]), .in24(dataBus[24]),
    .in25(dataBus[25]), .in26(dataBus[26]), .in27(dataBus[27]), .in28(dataBus[28]), .in29(dataBus[29]),
    .in30(dataBus[30]), .in31(dataBus[31]), .out(priority_encoder_1_out), .gs(priority_encoder_1_gs));  // open: en_out, en_in
  Multiplexer #(.width(5)) multiplexer_1 (
    .in0({5{1'b0}}), .in1(priority_encoder_1_out), .out(multiplexer_1_out), .sel(priority_encoder_1_gs));
  _7404 u_7404_1 (
    .pin13(priority_encoder_1_gs), .pin12(underFlow));  // open: pin1, pin2, pin3, pin4, pin5, pin6, pin11, pin10, pin9, pin8
  Subtractor #(.width(5)) subtractor_1 (.a({5{1'b1}}), .b(multiplexer_1_out), .out(selectBit));  // open: bin, bout
endmodule

module Truncer (
  input  [31:0] in32bit,
  input  [9:0] inExp,
  output [20:0] out21bit,
  output [9:0] outExp,
  output overflow
);

  wire adder_2_cout, n7432_1_pin1, n7432_1_pin2, n7432_1_pin3, n7432_2_pin1, n7432_2_pin2, n7432_2_pin3,
       n7432_2_pin6, n7432_3_pin8, n7432_3_pin11;
  wire [9:0] multiplexer_1_out;
  wire [20:0] adder_2_out, multiplexer_2_out;

  // Probe on in32bit[31]
  _7432 u_7432_1 (
    .pin1(n7432_1_pin1), .pin2(n7432_1_pin2), .pin3(n7432_1_pin3), .pin13(in32bit[0]), .pin12(in32bit[1]),
    .pin11(n7432_1_pin1), .pin10(in32bit[2]), .pin9(in32bit[3]), .pin8(n7432_1_pin2));  // open: pin4, pin5, pin6
  _7432 u_7432_2 (
    .pin1(n7432_2_pin1), .pin2(n7432_2_pin2), .pin3(n7432_2_pin3), .pin4(n7432_2_pin3), .pin5(n7432_1_pin3),
    .pin6(n7432_2_pin6), .pin13(in32bit[4]), .pin12(in32bit[5]), .pin11(n7432_2_pin1), .pin10(in32bit[6]),
    .pin9(in32bit[7]), .pin8(n7432_2_pin2));
  _7432 u_7432_3 (
    .pin13(n7432_2_pin6), .pin12(in32bit[10]), .pin11(n7432_3_pin11), .pin10(n7432_3_pin11),
    .pin9(in32bit[8]), .pin8(n7432_3_pin8));  // open: pin1, pin2, pin3, pin4, pin5, pin6
  Multiplexer #(.width(10)) multiplexer_1 (.in0({10{1'b0}}), .in1(10'h1), .out(multiplexer_1_out), .sel(adder_2_cout));
  Multiplexer #(.width(21)) multiplexer_2 (.in0({21{1'b0}}), .in1(21'h1), .out(multiplexer_2_out), .sel(n7432_3_pin8));
  Adder #(.width(10)) adder_1 (.a(multiplexer_1_out), .b(inExp), .out(outExp), .cout(overflow));  // open: cin
  Adder #(.width(21)) adder_2 (
    .a(in32bit[30:10]), .b(multiplexer_2_out), .out(adder_2_out), .cout(adder_2_cout));  // open: cin
  Multiplexer #(.width(21)) multiplexer_3 (.in0(in32bit[30:10]), .in1(adder_2_out), .out(out21bit), .sel(in32bit[9]));

  // Notes on the sheet:
  //   guard
  //   round
  //   sticky 0-7
  //   when sticky, round are 0, frac LSB tells if fraction needs to be made even.
  //   Rounding up will produce carry only when all fraction bits are 1. After rounding up, they'll all be 0, so simply incrementing the exponent keeping the fractions unshifted - will produce correct result.
  //   is_sticky
  //   truncated frac
  //   is_sticky_or_round_or_fraclsb
  //   rounded up frac
  //   if guard: round up; else: truncate
endmodule
